// Logisim project TD2_Ex5.circ as structural Verilog: 1 circuit, main circuit main
module main (
  input  [2:0] in_1,
  output out_2
);

  Multiplexer #(.select(3)) multiplexer_1 (
    .in0(1'b1), .in3(1'b1), .in5(1'b1), .in7(1'b1), .out(out_2), .sel(in_1));  // open: in1, in2, in4, in6
endmodule
