// Logisim project TD3_Ex1.circ as structural Verilog: 1 circuit, main circuit main
module main (
  input  S,
  input  R,
  output Q
);

  wire and_1_out, clock_1_out, d_ff_1_qn, not_1_out, or_1_out;

  not not_1 (not_1_out, R);
  and and_1 (and_1_out, Q, not_1_out);
  Clock clock_1 (.out(clock_1_out));
  or or_1 (or_1_out, S, and_1_out);
  D_Flip_Flop d_ff_1 (.D(or_1_out), .clk(clock_1_out), .Q(Q), .Qn(d_ff_1_qn));  // open: preset, reset
endmodule
