// Logisim project TD3_Ex2.circ as structural Verilog: 1 circuit, main circuit main
module main (
  input  R,
  output S1,
  output S2
);

  wire and_1_out, and_2_out, clock_1_out, d_ff_2_qn;

  Clock clock_1 (.out(clock_1_out));
  and and_1 (and_1_out, d_ff_2_qn, R);
  D_Flip_Flop d_ff_1 (.D(and_1_out), .clk(clock_1_out), .Q(S1));  // open: Qn, preset, reset
  and and_2 (and_2_out, R, S1);
  D_Flip_Flop d_ff_2 (.D(and_2_out), .clk(clock_1_out), .Q(S2), .Qn(d_ff_2_qn));  // open: preset, reset
endmodule
