// Logisim project TD3_Ex3.circ as structural Verilog: 1 circuit, main circuit main
module main (
  input  e,
  output S1,
  output S2
);

  wire clock_1_out, not_1_out, not_2_out, Q0_q, Q1_q;

  Clock clock_1 (.out(clock_1_out));
  D_Flip_Flop Q1 (.D(Q0_q), .clk(clock_1_out), .Q(Q1_q));  // open: Qn, preset, reset
  not not_1 (not_1_out, Q1_q);
  and and_1 (S1, not_1_out, Q0_q);
  D_Flip_Flop Q0 (.D(e), .clk(clock_1_out), .Q(Q0_q));  // open: Qn, preset, reset
  not not_2 (not_2_out, Q0_q);
  and and_2 (S2, Q1_q, not_2_out);
endmodule
