// Logisim project TD4_Ex1.circ as structural Verilog: 1 circuit, main circuit main
module main (
  input  BP,
  output LED
);

  wire and_1_out, clock_1_out, not_1_out, Q0_q, Q1_q, xor_1_out;

  xor xor_1 (xor_1_out, Q1_q, and_1_out);
  not not_1 (not_1_out, BP);
  Clock clock_1 (.out(clock_1_out));
  D_Flip_Flop Q1 (.D(xor_1_out), .clk(clock_1_out), .Q(Q1_q));  // open: Qn, preset, reset
  and and_1 (and_1_out, not_1_out, Q0_q);
  D_Flip_Flop Q0 (.D(BP), .clk(clock_1_out), .Q(Q0_q));  // open: Qn, preset, reset
  xor xor_2 (LED, Q1_q, Q0_q);
endmodule
